# Fritzing sketch esquemafritz (saved by Fritzing 0.9.3b)
breadboards: 1

parts:
  Componente1 = Arduino Mega 2560 (Rev3)
  R1 = Photocell (LDR) [package=THT]
  R2 = Resistor [tolerance=±5% resistance=10k package="2512 [SMD]"]
  LED1 = LED - 5mm [color="Red (633nm)" package="5 mm [THT]"]
  LED2 = LED - 5mm [color="Green (555nm)" package="5 mm [THT]"]
  R3 = Resistor [tolerance=±5% resistance=300 package="1206 [SMD]"]
  R4 = Resistor [tolerance=±5% resistance=300 package="1206 [SMD]"]
  S3 = Pushbutton [package="[THT]"]
  R5 = Resistor [tolerance=±5% resistance=10k package="2512 [SMD]"]
  R6 = Resistor [tolerance=±5% resistance=300 package="1206 [SMD]"]
  LED3 = RGB LED (com. anode, rbg) [package="5 mm [THT]"]
  R7 = Resistor [tolerance=±5% resistance=300 package="1206 [SMD]"]
  R8 = Resistor [tolerance=±5% resistance=300 package="1206 [SMD]"]
  SG1 = Buzzer 12mm [package=buzzer-12mm-ns]
  D1 = LED_BARGRAPH_10 [package=led_bargaph_10]
  R9 = Resistor [tolerance=±5% resistance=300 package="1206 [SMD]"]
  hc-sr1 = hc-sr04
  LCD2 = LCD screen
  LCM1602_IIC1 = LCM1602 IIC [part_number="LCM1602 IIC" chip_label="LCM1602 IIC" package="DIP (Dual Inline) [THT]"]

nets:
  N1: Componente1.A0, R1.pin_1, R2.Pin_0
  N2: Componente1.D21/SCL, LCM1602_IIC1.SDA
  N3: Componente1.D20/SDA, LCM1602_IIC1.SCL
  N4: Componente1.D13_PWM, SG1.2
  N5: Componente1.D11_PWM, LED1.cathode
  N6: Componente1.D10_PWM, LED2.cathode
  N7: Componente1.D6_PWM, S3.Pin_3, S3.Pin_4, R5.Pin_0
  N8: Componente1.D22, D1.G_C
  N9: Componente1.D23, D1.F_C
  N10: Componente1.D24, D1.E_C
  N11: Componente1.D25, D1.D_C
  N12: Componente1.D26, D1.B_C
  N13: Componente1.D27, D1.C_C
  N14: Componente1.D28, D1.A_C
  N15: Componente1.D40, hc-sr1.Trig
  N16: Componente1.D41, hc-sr1.Echo
  VCC: R1.pin_0, S3.Pin_1, S3.Pin_2, hc-sr1.VCC, LCM1602_IIC1.VCC
  N17: R2.Pin_1, R4.Pin_1, R5.Pin_1, R6.Pin_0, LED3.common_anode, R7.Pin_0, R8.Pin_0, SG1.1, LCM1602_IIC1.GND
  N18: LED1.anode, R3.Pin_0
  N19: LED2.anode, R4.Pin_0
  N20: R6.Pin_1, LED3.green_cathode
  N21: LED3.red_cathode, R8.Pin_1
  N22: LED3.blue_cathode, R7.Pin_1
  N23: D1.A_A, D1.B_A, D1.C_A, D1.D_A, D1.E_A, D1.F_A, D1.G_A, R9.Pin_1
  VSS: LCD2.VSS, LCM1602_IIC1.VSS
  VDD: LCD2.VDD, LCM1602_IIC1.VDD
  N24: LCD2.V0, LCM1602_IIC1.V0
  N25: LCD2.RS, LCM1602_IIC1.RS
  N26: LCD2.R/W, LCM1602_IIC1.RW
  N27: LCD2.E, LCM1602_IIC1.E
  N28: LCD2.DB0, LCM1602_IIC1.D0
  N29: LCD2.DB1, LCM1602_IIC1.D1
  N30: LCD2.DB2, LCM1602_IIC1.D2
  N31: LCD2.DB3, LCM1602_IIC1.D3
  N32: LCD2.DB4, LCM1602_IIC1.D4
  N33: LCD2.DB5, LCM1602_IIC1.D5
  N34: LCD2.DB6, LCM1602_IIC1.D6
  N35: LCD2.DB7, LCM1602_IIC1.D7
  N36: LCD2.LED+, LCM1602_IIC1.A
  N37: LCD2.LED-, LCM1602_IIC1.K
  N38: LCM1602_IIC1.LED_A, LCM1602_IIC1.LED_B

custom parts:
  LCM1602 IIC: I2C-Module to use a 1602 or 2004 LCD on with the wire.h libory Serial LCD Modul
